# Fritzing sketch esp8266_ldr (saved by Fritzing 0.9.3b)

parts:
  U2 = NodeMCU V1.0
  R6 = Resistor [tolerance=±5% resistance=1k package=THT]
  R7 = Resistor [tolerance=±5% resistance=1k package=THT]
  R8 = Resistor [tolerance=±5% resistance=1k package=THT]
  R9 = Resistor [tolerance=±5% resistance=1k package=THT]
  R10 = Resistor [tolerance=±5% resistance=1k package=THT]
  R11 = Photocell (LDR) [package=THT]
  R12 = Resistor [tolerance=±5% resistance=1k package=THT]
  LED1 = LED - 3mm [color="Red (633nm)" package="3 mm [THT]"]
  LED4 = LED - 3mm [color="Red (633nm)" package="3 mm [THT]"]
  LED3 = LED - 3mm [color="Red (633nm)" package="3 mm [THT]"]
  LED2 = LED - 3mm [color="Red (633nm)" package="3 mm [THT]"]
  LED5 = LED - 3mm [color="Red (633nm)" package="3 mm [THT]"]

nets:
  N1: U2.D0, R6.Pin_1
  N2: U2.D1, R7.Pin_1
  N3: U2.D2, R8.Pin_1
  N4: U2.D3, R9.Pin_1
  N5: U2.D4, R10.Pin_1
  N6: U2.GND, LED5.cathode
  N7: U2.3V3, R11.pin_1
  N8: U2.A0, R11.pin_0, R12.Pin_0
  N9: R6.Pin_0, LED5.anode
  N10: R7.Pin_0, LED4.anode
  N11: R8.Pin_0, LED3.anode
  N12: R9.Pin_0, LED2.anode
  N13: R10.Pin_0, LED1.anode

custom parts:
  NodeMCU V1.0: ESP9266 based NodeMCU
